# Fritzing sketch feather3 (saved by Fritzing 0.9.1b)

parts:
  J5 = female pin header, 16 pins [form="♀ (female)"]
  J6 = female pin header, 7 pins [form="♀ (female)"]
  J7 = female pin header, 12 pins [form="♀ (female)"]
  J8 = female pin header, 7 pins [form="♀ (female)"]
  J9 = Screw terminal - 2 pins [package=THT]  # not connected
  U12 = mystery part, 3 pins [chip_label=TSR12450]  # not connected
  C6 = Electrolytic Capacitor [capacitance=22µF package="100 mil [THT, electrolytic]"]  # not connected

nets:
  N1: J5.pin13, J5.pin14, J8.pin5
  N2: J5.pin15, J5.pin16, J6.pin1
  N3: J6.pin7, J7.pin3
  N4: J7.pin1, J8.pin2
  N5: J7.pin2, J8.pin4

notes:
  Light Sensor Suite
